# Fritzing sketch carm (saved by Fritzing 0.9.3b)

parts:
  S1 = H-Bridge with L298N
  BATT1 = 4xAA Switchable Battery Pack w/Bare Wire
  BATT2 = 4xAA Switchable Battery Pack w/Bare Wire
  PWM1 = PCA9685 16x12-bit PWM Breakout
  Raspberry_Pi_1 = Raspberry Pi 3 [part_number=RPI-3-V1.2]
  M1 = DC Motor
  M2 = DC Motor
  J2 = Basic Servo
  J3 = Basic Servo
  J4 = Basic Servo
  J5 = Basic Servo

nets:
  N1: S1.12V, BATT1.POS
  GND: S1.GND, BATT1.NEG, BATT2.NEG, PWM1.no_name_yet#601, PWM1.no_name_yet#701, PWM1.no_name_yet#1012, PWM1.no_name_yet#1013, PWM1.no_name_yet#1014, PWM1.no_name_yet#1015, Raspberry_Pi_1.GND
  N2: S1.IN1, Raspberry_Pi_1.GPIO12
  N3: S1.IN2, Raspberry_Pi_1.GPIO16
  N4: S1.IN3, Raspberry_Pi_1.GPIO5
  N5: S1.IN4, Raspberry_Pi_1.GPIO6
  N6: S1.M1-01, M1.pin_2
  N7: S1.M1-02, M1.pin_1
  N8: S1.M2-01, M2.pin_2
  N9: S1.M2-02, M2.pin_1
  N10: BATT2.POS, PWM1.no_name_yet#112, PWM1.no_name_yet#113, PWM1.no_name_yet#114, PWM1.no_name_yet#115, PWM1.no_name_yet#706
  N11: PWM1.no_name_yet#12, J4.pulse
  N12: PWM1.no_name_yet#13, J3.pulse
  N13: PWM1.no_name_yet#14, J2.pulse
  N14: PWM1.no_name_yet#15, J5.pulse
  N15: PWM1.no_name_yet#603, Raspberry_Pi_1.GPIO3
  N16: PWM1.no_name_yet#604, Raspberry_Pi_1.GPIO2
  N17: PWM1.no_name_yet#605, Raspberry_Pi_1.3v3

custom parts:
  H-Bridge with L298N: h-bridge
  4xAA Switchable Battery Pack w/Bare Wire: 4xAA Switchable Battery Pack with Bare Wire connection
