# Fritzing sketch dc_motor_hookup (saved by Fritzing 0.9.3b)
breadboards: 1

parts:
  S1 = H-Bridge with L298N
  BATT1 = 4xAA Switchable Battery Pack w/Bare Wire
  Raspberry_Pi_1 = Raspberry Pi 3 [part_number=RPI-3-V1.2]
  M1 = DC Motor
  M2 = DC Motor

nets:
  N1: S1.12V, BATT1.POS
  GND: S1.GND, BATT1.NEG, Raspberry_Pi_1.GND
  N2: S1.5V, S1.ENA
  N3: S1.IN1, Raspberry_Pi_1.GPIO24
  N4: S1.IN2, Raspberry_Pi_1.GPIO23
  N5: S1.IN3, Raspberry_Pi_1.GPIO12
  N6: S1.IN4, Raspberry_Pi_1.GPIO16
  N7: S1.M1-01, M1.pin_2
  N8: S1.M1-02, M1.pin_1
  N9: S1.M2-01, M2.pin_2
  N10: S1.M2-02, M2.pin_1

custom parts:
  H-Bridge with L298N: h-bridge
  4xAA Switchable Battery Pack w/Bare Wire: 4xAA Switchable Battery Pack with Bare Wire connection
